# Fritzing sketch display_ldr_relay (saved by Fritzing 0.8.7b)
breadboards: 1

parts:
  LCD1 = LCD screen
  R2 = Resistor [tolerance=±5% resistance=2.2k package=THT]
  R4 = Photocell (LDR) [package=THT]
  Q1 = NPN-Transistor [package="TO92 [THT]"]
  R5 = Resistor [tolerance=±5% resistance=2.2k package=THT]
  Componente1 = Arduino Uno (Rev3)
  U1 = RELAY-2 [package=relay-g5v]
  D2 = Rectifier Diode [part_number=1N4001 package="300 mil [THT]"]

nets:
  VSS: LCD1.VSS, Componente1.GND
  VDD: LCD1.VDD, Componente1.5V
  N1: LCD1.RS, Componente1.D12/MISO
  N2: LCD1.E, Componente1.D11_PWM/MOSI
  N3: LCD1.DB4, Componente1.D5_PWM
  N4: LCD1.DB5, Componente1.D4
  N5: LCD1.DB6, Componente1.D3_PWM
  N6: LCD1.DB7, Componente1.D2
  N7: R2.Pin_0, R4.pin_1, Componente1.A0
  N8: Q1.E, U1.5, D2.anode
  N9: Q1.B, R5.Pin_0
  N10: R5.Pin_1, Componente1.D8
  N11: U1.6, D2.cathode
