# Fritzing sketch display_message (saved by Fritzing 0.8.7b)

parts:
  LCD1 = LCD screen
  Componente1 = Arduino Uno (Rev3)

nets:
  VSS: LCD1.VSS, LCD1.V0, LCD1.R/W, LCD1.LED-, Componente1.GND
  VDD: LCD1.VDD, LCD1.LED+, Componente1.5V
  N1: LCD1.RS, Componente1.D12/MISO
  N2: LCD1.E, Componente1.D11_PWM/MOSI
  N3: LCD1.DB4, Componente1.D5_PWM
  N4: LCD1.DB5, Componente1.D4
  N5: LCD1.DB6, Componente1.D3_PWM
  N6: LCD1.DB7, Componente1.D2
