# Fritzing sketch display_potentiometer (saved by Fritzing 0.8.7b)
breadboards: 1

parts:
  LCD1 = LCD screen
  R1 = Rotary Potentiometer (Small) [maximum_resistance=100kΩ package=THT]
  Componente1 = Arduino Uno (Rev3)

nets:
  VSS: LCD1.VSS, Componente1.GND
  VDD: LCD1.VDD, Componente1.5V
  N1: LCD1.RS, Componente1.D12/MISO
  N2: LCD1.E, Componente1.D11_PWM/MOSI
  N3: LCD1.DB4, Componente1.D5_PWM
  N4: LCD1.DB5, Componente1.D4
  N5: LCD1.DB6, Componente1.D3_PWM
  N6: LCD1.DB7, Componente1.D2
  N7: R1.wiper, Componente1.A0
