# Fritzing sketch display_temperature_buzzer (saved by Fritzing 0.8.7b)
breadboards: 1

parts:
  LCD1 = LCD screen
  R2 = Resistor [tolerance=±5% resistance=4.7k package=THT]  # not connected
  J1 = Piezo Speaker
  R3 = Resistor [tolerance=±5% resistance=100 package=THT]
  Componente1 = Arduino Uno (Rev3)
  DS1 = DS18B20 1-Wire Temperature Sensor [part_number=DS18B20]

nets:
  VSS: LCD1.VSS, Componente1.GND
  VDD: LCD1.VDD, Componente1.5V
  N1: LCD1.RS, Componente1.D12/MISO
  N2: LCD1.E, Componente1.D11_PWM/MOSI
  N3: LCD1.DB4, Componente1.D5_PWM
  N4: LCD1.DB5, Componente1.D4
  N5: LCD1.DB6, Componente1.D3_PWM
  N6: LCD1.DB7, Componente1.D2
  N7: J1.pin1, DS1.GND
  N8: J1.pin2, R3.Pin_0
  N9: R3.Pin_1, Componente1.D13/SCK
  N10: Componente1.D8, DS1.DQ
