# Fritzing sketch fade (saved by Fritzing 0.8.7b)
breadboards: 1

parts:
  LED1 = LED - 5mm [color="Red (633nm)" package="5 mm [THT]"]
  R2 = Resistor [tolerance=±5% resistance=330 package=THT]
  R1 = Rotary Potentiometer (Small) [maximum_resistance=100kΩ package=THT]
  Componente1 = Arduino Uno (Rev3)

nets:
  N1: LED1.anode, R2.Pin_0
  N2: R2.Pin_1, Componente1.D3_PWM
  N3: R1.leg1, Componente1.5V
  N4: R1.wiper, Componente1.A0
  N5: R1.leg2, Componente1.GND
