# Fritzing sketch ledbar (saved by Fritzing 0.8.7b)
breadboards: 1

parts:
  LED2 = LED - 5mm [color="Red (635nm)" package="5 mm [THT]"]
  LED3 = LED - 5mm [color="Red (635nm)" package="5 mm [THT]"]
  LED4 = LED - 5mm [color="Yellow (595nm)" package="5 mm [THT]"]
  LED5 = LED - 5mm [color="Yellow (595nm)" package="5 mm [THT]"]
  LED6 = LED - 5mm [color="Green (565nm)" package="5 mm [THT]"]
  LED8 = LED - 5mm [color="Green (565nm)" package="5 mm [THT]"]
  LED1 = smd LED [color="Red (633nm)" package="0603 [SMD]"]
  LED1_2 = LED - 5mm [color="Red (635nm)" package="5 mm [THT]"]
  R2 = Resistor [tolerance=±5% resistance=150 package=THT]
  LED7 = smd LED [color="Green (565nm)" package="0603 [SMD]"]
  LED7_2 = LED - 5mm [color="Green (565nm)" package="5 mm [THT]"]
  Componente1 = Arduino Uno (Rev3)
  R3 = Resistor [tolerance=±5% resistance=150 package=THT]
  R4 = Resistor [tolerance=±5% resistance=150 package=THT]
  R5 = Resistor [tolerance=±5% resistance=150 package=THT]
  R6 = Resistor [tolerance=±5% resistance=150 package=THT]
  R7 = Resistor [tolerance=±5% resistance=150 package=THT]
  R8 = Resistor [tolerance=±5% resistance=150 package=THT]
  R9 = Resistor [tolerance=±5% resistance=150 package=THT]

nets:
  N1: LED2.cathode, LED3.cathode, LED4.cathode, LED5.cathode, LED6.cathode, LED8.cathode, LED1.cathode, LED1_2.cathode, LED7.cathode, LED7_2.cathode, Componente1.GND
  N2: LED2.anode, R3.Pin_0
  N3: LED3.anode, R4.Pin_0
  N4: LED4.anode, R5.Pin_0
  N5: LED5.anode, R6.Pin_0
  N6: LED6.anode, R7.Pin_0
  N7: LED8.anode, R9.Pin_0
  N8: LED1.anode, LED1_2.anode, R2.Pin_0
  N9: R2.Pin_1, Componente1.D9_PWM
  N10: LED7.anode, LED7_2.anode, R8.Pin_0
  N11: Componente1.D8, R3.Pin_1
  N12: Componente1.D2, R9.Pin_1
  N13: Componente1.D3_PWM, R8.Pin_1
  N14: Componente1.D4, R7.Pin_1
  N15: Componente1.D5_PWM, R6.Pin_1
  N16: Componente1.D6_PWM, R5.Pin_1
  N17: Componente1.D7, R4.Pin_1
