# Fritzing sketch ledbar_encoder (saved by Fritzing 0.8.7b)
breadboards: 1

parts:
  LED2 = LED - 5mm [color="Red (635nm)" package="5 mm [THT]"]
  LED3 = LED - 5mm [color="Red (635nm)" package="5 mm [THT]"]
  LED4 = LED - 5mm [color="Yellow (595nm)" package="5 mm [THT]"]
  LED5 = LED - 5mm [color="Yellow (595nm)" package="5 mm [THT]"]
  LED6 = LED - 5mm [color="Green (565nm)" package="5 mm [THT]"]
  LED8 = LED - 5mm [color="Green (565nm)" package="5 mm [THT]"]
  LED1 = smd LED [color="Red (633nm)" package="0603 [SMD]"]
  LED1_2 = LED - 5mm [color="Red (635nm)" package="5 mm [THT]"]
  R2 = Resistor [tolerance=±5% resistance=1k package=THT]
  R3 = Resistor [tolerance=±5% resistance=1k package=THT]
  R4 = Resistor [tolerance=±5% resistance=1k package=THT]
  R5 = Resistor [tolerance=±5% resistance=1k package=THT]
  R6 = Resistor [tolerance=±5% resistance=1k package=THT]
  R7 = Resistor [tolerance=±5% resistance=1k package=THT]
  R8 = Resistor [tolerance=±5% resistance=1k package=THT]
  R9 = Resistor [tolerance=±5% resistance=1k package=THT]
  LED7 = smd LED [color="Green (565nm)" package="0603 [SMD]"]
  LED7_2 = LED - 5mm [color="Green (565nm)" package="5 mm [THT]"]
  Componente1 = Arduino Uno (Rev3)
  ENCODER1 = Rotary Encoder with Knob

nets:
  N1: LED2.cathode, LED3.cathode, LED4.cathode, LED5.cathode, LED6.cathode, LED8.cathode, LED1.cathode, LED1_2.cathode, LED7.cathode, LED7_2.cathode, ENCODER1.no_name_yet#2
  N2: LED2.anode, R3.Pin_0
  N3: LED3.anode, R4.Pin_0
  N4: LED4.anode, R5.Pin_0
  N5: LED5.anode, R6.Pin_0
  N6: LED6.anode, R7.Pin_0
  N7: LED8.anode, R9.Pin_0
  N8: LED1.anode, LED1_2.anode, R2.Pin_0
  N9: R2.Pin_1, Componente1.D9_PWM
  N10: R3.Pin_1, Componente1.D8
  N11: R4.Pin_1, Componente1.D7
  N12: R5.Pin_1, Componente1.D6_PWM
  N13: R6.Pin_1, Componente1.D5_PWM
  N14: R7.Pin_1, Componente1.D4
  N15: R8.Pin_0, LED7.anode, LED7_2.anode
  N16: R8.Pin_1, Componente1.D3_PWM
  N17: R9.Pin_1, Componente1.D2
  N18: Componente1.A0, ENCODER1.no_name_yet#3
  N19: Componente1.A1, ENCODER1.no_name_yet#1

custom parts:
  Rotary Encoder with Knob: Rotary Encoder with 1/4" Shaft and Knob
