# Fritzing sketch rgb_encoder (saved by Fritzing 0.8.7b)
breadboards: 1

parts:
  Part1 = Arduino Uno (Rev3)
  R1 = Resistor [tolerance=±5% resistance=220 package=THT]
  LED1 = RGB LED (com. anode, rbg) [package="5 mm [THT]"]
  R2 = Resistor [tolerance=±5% resistance=220 package=THT]
  R3 = Resistor [tolerance=±5% resistance=220 package=THT]
  LED2 = LED - 5mm [color="Green (565nm)" package="5 mm [THT]"]
  LED3 = LED - 5mm [color="Blue (430nm)" package="5 mm [THT]"]
  LED4 = LED - 5mm [color="Red (633nm)" package="5 mm [THT]"]
  R4 = Resistor [tolerance=±5% resistance=220 package=THT]
  R5 = Resistor [tolerance=±5% resistance=220 package=THT]
  R6 = Resistor [tolerance=±5% resistance=220 package=THT]
  ENCODER1 = Rotary Encoder with Knob

nets:
  N1: Part1.A0, ENCODER1.no_name_yet#1
  N2: Part1.A1, ENCODER1.no_name_yet#3
  N3: Part1.D8, R5.Pin_1
  N4: Part1.D9_PWM, R4.Pin_1
  N5: Part1.D10_PWM/SS, R6.Pin_1
  N6: Part1.D3_PWM, R1.Pin_1
  N7: Part1.D5_PWM, R2.Pin_1
  N8: Part1.D6_PWM, R3.Pin_1
  N9: Part1.GND, LED1.common_anode, LED2.cathode, LED3.cathode, LED4.cathode, ENCODER1.no_name_yet#2, ENCODER1.no_name_yet#4
  N10: R1.Pin_0, LED1.green_cathode
  N11: LED1.red_cathode, R3.Pin_0
  N12: LED1.blue_cathode, R2.Pin_0
  N13: LED2.anode, R4.Pin_0
  N14: LED3.anode, R5.Pin_0
  N15: LED4.anode, R6.Pin_0

custom parts:
  Rotary Encoder with Knob: Rotary Encoder with 1/4" Shaft and Knob
