# Fritzing sketch servo_encoder (saved by Fritzing 0.8.7b)
breadboards: 1

parts:
  Part1 = Arduino Uno (Rev3)
  J1 = Basic Servo
  ENCODER1 = Rotary Encoder with Knob

nets:
  N1: Part1.D9_PWM, J1.pulse
  N2: Part1.D5_PWM, ENCODER1.no_name_yet#3
  N3: Part1.D6_PWM, ENCODER1.no_name_yet#1
  5V: Part1.5V, J1.vcc
  GND: Part1.GND, J1.gnd, ENCODER1.no_name_yet#2

custom parts:
  Rotary Encoder with Knob: Rotary Encoder with 1/4" Shaft and Knob
